# Fritzing sketch Tmst Sketch (saved by Fritzing 0.9.3b)
breadboards: 1

parts:
  Part1 = Arduino Nano (Rev3.0)
  U1 = DC-DC 2-24V Step Up Booster [package=THT]
  S2 = SWITCH-DPDT [package=os]
  R1 = TRIMPOT [package=trimpot_pth_s3_lock]
  C1 = Ceramic Capacitor [capacitance="100 nF" package="0603 [SMD, multilayer]"]
  R2 = Resistor [tolerance=±5% resistance=10k package="0805 [SMD]"]
  J1 = Dagu DGServo 9g header connector (female) [package=THT]
  J2 = Dagu DGServo 9g header connector (female) [package=THT]
  J3 = Dagu DGServo 9g header connector (female) [package=THT]
  J4 = Dagu DGServo 9g header connector (female) [package=THT]

nets:
  GND: Part1.GND, U1.pin2, U1.pin4, R1.CW, C1.0, R2.Pin_1, J1.gnd, J2.gnd, J3.gnd, J4.gnd
  N1: Part1.D5, S2.5, R2.Pin_0
  N2: Part1.D6, J1.pulse
  N3: Part1.D7, J2.pulse
  N4: Part1.D8, J3.pulse
  N5: Part1.D9, J4.pulse
  N6: Part1.VIN, U1.pin1
  N7: Part1.5V, S2.6, R1.CCW, C1.1
  N8: Part1.A0, R1.WIPER
  VCC: J1.Vcc, J2.Vcc, J3.Vcc, J4.Vcc

custom parts:
  DC-DC 2-24V Step Up Booster: Convertisseur DC-DC 2-24V 2A
